// Logisim project Cache.circ as structural Verilog: 8 circuits, main circuit implementation
module implementation (
  input  [9:0] CpuAddressIn,
  input  CpuReadIn,
  input  CpuWriteIn,
  input  [7:0] CpuWriteValueIn,
  input  [31:0] LineFromMemIn,
  input  ClkIn,
  output ReadyOut,
  output DidContainOut,
  output [7:0] ByteReadOut,
  output [7:0] MemAddressOut,
  output MemReadOut,
  output MemWriteOut,
  output [31:0] Line2MemOut
);

  Cache cache_1 (
    .CpuAddressIn(CpuAddressIn), .CpuReadIn(CpuReadIn), .CpuWriteIn(CpuWriteIn),
    .CpuWriteValueIn(CpuWriteValueIn), .LineFromMemIn(LineFromMemIn), .ClkIn(ClkIn), .ReadyOut(ReadyOut),
    .DidContainOut(DidContainOut), .ByteReadOut(ByteReadOut), .MemAddressOut(MemAddressOut),
    .MemReadOut(MemReadOut), .MemWriteOut(MemWriteOut), .Line2MemOut(Line2MemOut));

  // Other names for the same wires on the sheet: ByteRead[7:0] = ByteReadOut; clk = ClkIn;
  //   CpuAddress[9:0] = CpuAddressIn; CpuRead = CpuReadIn; CpuWrite = CpuWriteIn;
  //   CpuWriteValue[7:0] = CpuWriteValueIn; DidContain = DidContainOut; Line2Mem[31:0] = Line2MemOut;
  //   LineFromMem[31:0] = LineFromMemIn; MemAddress[7:0] = MemAddressOut; MemRead = MemReadOut;
  //   MemWrite = MemWriteOut; Ready = ReadyOut
endmodule

module Cache (
  input  [9:0] CpuAddressIn,
  input  CpuReadIn,
  input  CpuWriteIn,
  input  [7:0] CpuWriteValueIn,
  input  [31:0] LineFromMemIn,
  input  ClkIn,
  output ReadyOut,
  output DidContainOut,
  output [7:0] ByteReadOut,
  output [7:0] MemAddressOut,
  output MemReadOut,
  output MemWriteOut,
  output [31:0] Line2MemOut
);

  wire Active0, Active1, CacheActive, CpuReadIn_t, CpuWriteIn_t, DidContain0, DidContain1, DidContainInput,
       Dirty, Dirty0, Dirty1, IncomingData, Initialize, not_1_out, SetBits, StoredCpuRead, StoredCpuWrite,
       UpdateAge, Write;
  wire [1:0] OffsetBits;
  wire [7:0] ByteRead0, ByteRead1, MemAddress0, MemAddress1, StoredCpuWriteValue;
  wire [9:3] StoredCpuAddress;
  wire [31:0] Line2Mem0, Line2Mem1;

  Register #(.width(10)) register_1 (
    .D(CpuAddressIn), .en(ReadyOut), .clk(ClkIn), .Q({StoredCpuAddress, SetBits, OffsetBits}));  // open: clr
  Register #(.width(1)) register_2 (.D(CpuReadIn), .en(ReadyOut), .clk(ClkIn), .Q(StoredCpuRead));  // open: clr
  Register #(.width(1)) register_3 (.D(CpuWriteIn), .en(ReadyOut), .clk(ClkIn), .Q(StoredCpuWrite));  // open: clr
  Register register_4 (.D(CpuWriteValueIn), .en(ReadyOut), .clk(ClkIn), .Q(StoredCpuWriteValue));  // open: clr
  Multiplexer #(.enable("false")) multiplexer_1 (
    .in0(StoredCpuRead), .in1(CpuReadIn), .out(CpuReadIn_t), .sel(ReadyOut));
  Multiplexer #(.enable("false")) multiplexer_2 (
    .in0(StoredCpuWrite), .in1(CpuWriteIn), .out(CpuWriteIn_t), .sel(ReadyOut));
  or or_1 (CacheActive, StoredCpuRead, StoredCpuWrite);
  and and_1 (Active0, CacheActive, not_1_out);
  not not_1 (not_1_out, SetBits);
  and and_2 (Active1, CacheActive, SetBits);
  FSMController fsmcontroller_1 (
    .CpuRead(CpuReadIn_t), .CpuWrite(CpuWriteIn_t), .didContain(DidContainInput), .Dirty(Dirty),
    .ClkIn(ClkIn), .Ready(ReadyOut), .Initialize(Initialize), .MemReadOut(MemReadOut),
    .MemWriteOut(MemWriteOut), .UpdateAge(UpdateAge), .IncomingData(IncomingData), .WriteOut(Write));
  Set set0 (
    .Active(Active0), .Initialize(Initialize), .UpdateAge(UpdateAge), .OffsetBits(OffsetBits),
    .SetBits(SetBits), .TagBits(StoredCpuAddress), .CpuReadIn(CpuReadIn), .CpuWriteIn(CpuWriteIn),
    .Write(Write), .ClearDirty(MemWriteOut), .IncomingData(IncomingData),
    .CpuWriteValueIn(StoredCpuWriteValue), .LineFromMemIn(LineFromMemIn), .ClkIn(ClkIn),
    .DidContainOut(DidContain0), .Dirty(Dirty0), .ByteReadOut(ByteRead0), .MemAddressOut(MemAddress0),
    .Line2MemOut(Line2Mem0));
  Multiplexer #(.enable("false")) multiplexer_3 (
    .in0(DidContain0), .in1(DidContain1), .out(DidContainInput), .sel(SetBits));
  Multiplexer #(.enable("false")) multiplexer_4 (.in0(Dirty0), .in1(Dirty1), .out(Dirty), .sel(SetBits));
  Multiplexer #(.enable("false"), .width(8)) multiplexer_5 (
    .in0(ByteRead0), .in1(ByteRead1), .out(ByteReadOut), .sel(SetBits));
  Set set1 (
    .Active(Active1), .Initialize(Initialize), .UpdateAge(UpdateAge), .OffsetBits(OffsetBits),
    .SetBits(SetBits), .TagBits(StoredCpuAddress), .CpuReadIn(CpuReadIn), .CpuWriteIn(CpuWriteIn),
    .Write(Write), .ClearDirty(MemWriteOut), .IncomingData(IncomingData),
    .CpuWriteValueIn(StoredCpuWriteValue), .LineFromMemIn(LineFromMemIn), .ClkIn(ClkIn),
    .DidContainOut(DidContain1), .Dirty(Dirty1), .ByteReadOut(ByteRead1), .MemAddressOut(MemAddress1),
    .Line2MemOut(Line2Mem1));
  Register #(.width(1)) register_5 (.D(DidContainInput), .en(Initialize), .clk(ClkIn), .Q(DidContainOut));  // open: clr
  Multiplexer #(.enable("false"), .width(8)) multiplexer_6 (
    .in0(MemAddress0), .in1(MemAddress1), .out(MemAddressOut), .sel(SetBits));
  Multiplexer #(.enable("false"), .width(32)) multiplexer_7 (
    .in0(Line2Mem0), .in1(Line2Mem1), .out(Line2MemOut), .sel(SetBits));

  // Other names for the same wires on the sheet: ByteRead[7:0] = ByteReadOut; clk = ClkIn;
  //   CpuAddress[9:0] = CpuAddressIn; CpuRead = CpuReadIn; CpuWrite = CpuWriteIn;
  //   CpuWriteValue[7:0] = CpuWriteValueIn; Line2Mem[31:0] = Line2MemOut; LineFromMem[31:0] = LineFromMemIn;
  //   MemAddress[7:0] = MemAddressOut; MemRead = MemReadOut; ClearDirty = MemWriteOut; MemWrite = MemWriteOut;
  //   Ready = ReadyOut; StoredCpuAddress[2:0] = {SetBits, OffsetBits}; TagBits[6:0] = StoredCpuAddress
endmodule

module Set (
  input  Active,
  input  Initialize,
  input  UpdateAge,
  input  [1:0] OffsetBits,
  input  SetBits,
  input  [6:0] TagBits,
  input  CpuReadIn,
  input  CpuWriteIn,
  input  Write,
  input  ClearDirty,
  input  IncomingData,
  input  [7:0] CpuWriteValueIn,
  input  [31:0] LineFromMemIn,
  input  ClkIn,
  output DidContainOut,
  output Dirty,
  output [7:0] ByteReadOut,
  output [7:0] MemAddressOut,
  output [31:0] Line2MemOut
);

  wire Active0, Active1, Active2, and_1_out, and_2_out, and_3_out, comparator_1_eq, comparator_2_eq,
       comparator_3_eq, Dirty0, Dirty1, Dirty2, inWay0, inWay1, inWay2, multiplexer_1_out, multiplexer_6_out,
       multiplexer_8_out, multiplexer_12_out, multiplexer_16_out, not_1_out, toWay0, toWay1, toWay2,
       UpdateWays, Valid0, Valid1, Valid2;
  wire [1:0] Age0, Age0Out, Age1, Age1Out, Age2, Age2Out, AgeAccessed, multiplexer_2_out, multiplexer_3_out,
       multiplexer_4_out, multiplexer_5_out;
  wire [6:0] CurrTagBits0, CurrTagBits1, CurrTagBits2;
  wire [7:0] ByteReadOut0, ByteReadOut1, ByteReadOut2, MemAddress0, MemAddress1, MemAddress2,
       multiplexer_9_out, multiplexer_10_out, multiplexer_13_out, multiplexer_14_out;
  wire [31:0] Line2Mem0, Line2Mem1, Line2Mem2, multiplexer_11_out, multiplexer_15_out;

  Register #(.width(2)) u_age0 (.D(Age0Out), .en(and_1_out), .clk(ClkIn), .Q(Age0));  // open: clr
  and and_1 (and_1_out, UpdateAge, Active);
  Register #(.width(2)) u_age1 (.D(Age1Out), .en(and_2_out), .clk(ClkIn), .Q(Age1));  // open: clr
  and and_2 (and_2_out, UpdateAge, Active);
  Register #(.width(2)) u_age2 (.D(Age2Out), .en(and_3_out), .clk(ClkIn), .Q(Age2));  // open: clr
  and and_3 (and_3_out, UpdateAge, Active);
  Comparator #(.width(7)) comparator_1 (.a(TagBits), .b(CurrTagBits0), .eq(comparator_1_eq));  // open: gt, lt
  Comparator #(.width(7)) comparator_2 (.a(TagBits), .b(CurrTagBits1), .eq(comparator_2_eq));  // open: gt, lt
  Comparator #(.width(7)) comparator_3 (.a(TagBits), .b(CurrTagBits2), .eq(comparator_3_eq));  // open: gt, lt
  and and_4 (inWay0, Valid0, comparator_1_eq);
  and and_5 (inWay1, Valid1, comparator_2_eq);
  and and_6 (inWay2, Valid2, comparator_3_eq);
  AgeAccessedLogic ageaccessedlogic_1 (
    .AgeOfAccessed(AgeAccessed), .Age0(Age0), .Age1(Age1), .Age2(Age2), .Age0Out(Age0Out), .Age1Out(Age1Out),
    .Age2Out(Age2Out));
  Multiplexer #(.enable("false")) multiplexer_1 (.in0(toWay0), .in1(inWay0), .out(multiplexer_1_out), .sel(UpdateWays));
  Multiplexer #(.enable("false"), .width(2)) multiplexer_2 (
    .in0(2'b00), .in1(Age0), .out(multiplexer_2_out), .sel(inWay0));
  not not_1 (not_1_out, Initialize);
  and and_7 (UpdateWays, Active, not_1_out, DidContainOut);
  and and_8 (Active0, multiplexer_1_out, Active);
  Multiplexer #(.enable("false"), .width(2)) multiplexer_3 (
    .in0(multiplexer_2_out), .in1(Age1), .out(multiplexer_3_out), .sel(inWay1));
  Comparator #(.width(2)) comparator_4 (.a(Age0), .b(2'b10), .eq(toWay0));  // open: gt, lt
  Comparator #(.width(2)) comparator_5 (.a(Age1), .b(2'b10), .eq(toWay1));  // open: gt, lt
  Comparator #(.width(2)) comparator_6 (.a(Age2), .b(2'b10), .eq(toWay2));  // open: gt, lt
  Multiplexer #(.enable("false"), .width(2)) multiplexer_4 (
    .in0(multiplexer_3_out), .in1(Age2), .out(multiplexer_4_out), .sel(inWay2));
  Multiplexer #(.enable("false"), .width(2)) multiplexer_5 (
    .in0(2'b10), .in1(multiplexer_4_out), .out(multiplexer_5_out), .sel(DidContainOut));
  Multiplexer #(.enable("false")) multiplexer_6 (.in0(toWay1), .in1(inWay1), .out(multiplexer_6_out), .sel(UpdateWays));
  and and_9 (Active1, multiplexer_6_out, Active);
  Multiplexer #(.enable("false"), .width(2)) multiplexer_7 (
    .in0(multiplexer_5_out), .in1(2'b00), .out(AgeAccessed), .sel(Initialize));
  Multiplexer #(.enable("false")) multiplexer_8 (.in0(1'b0), .in1(Dirty0), .out(multiplexer_8_out), .sel(Active0));
  Multiplexer #(.enable("false"), .width(8)) multiplexer_9 (
    .in0({8{1'b0}}), .in1(ByteReadOut0), .out(multiplexer_9_out), .sel(Active0));
  Multiplexer #(.enable("false"), .width(8)) multiplexer_10 (
    .in0({8{1'b0}}), .in1(MemAddress0), .out(multiplexer_10_out), .sel(Active0));
  Multiplexer #(.enable("false"), .width(32)) multiplexer_11 (
    .in0({32{1'b0}}), .in1(Line2Mem0), .out(multiplexer_11_out), .sel(Active0));
  Multiplexer #(.enable("false")) multiplexer_12 (
    .in0(multiplexer_8_out), .in1(Dirty1), .out(multiplexer_12_out), .sel(Active1));
  Multiplexer #(.enable("false"), .width(8)) multiplexer_13 (
    .in0(multiplexer_9_out), .in1(ByteReadOut1), .out(multiplexer_13_out), .sel(Active1));
  Multiplexer #(.enable("false"), .width(8)) multiplexer_14 (
    .in0(multiplexer_10_out), .in1(MemAddress1), .out(multiplexer_14_out), .sel(Active1));
  Multiplexer #(.enable("false"), .width(32)) multiplexer_15 (
    .in0(multiplexer_11_out), .in1(Line2Mem1), .out(multiplexer_15_out), .sel(Active1));
  or or_1 (DidContainOut, inWay0, inWay1, inWay2);
  Multiplexer #(.enable("false")) multiplexer_16 (
    .in0(toWay2), .in1(inWay2), .out(multiplexer_16_out), .sel(UpdateWays));
  Multiplexer #(.enable("false")) multiplexer_17 (.in0(multiplexer_12_out), .in1(Dirty2), .out(Dirty), .sel(Active2));
  Multiplexer #(.enable("false"), .width(8)) multiplexer_18 (
    .in0(multiplexer_13_out), .in1(ByteReadOut2), .out(ByteReadOut), .sel(Active2));
  Multiplexer #(.enable("false"), .width(8)) multiplexer_19 (
    .in0(multiplexer_14_out), .in1(MemAddress2), .out(MemAddressOut), .sel(Active2));
  Multiplexer #(.enable("false"), .width(32)) multiplexer_20 (
    .in0(multiplexer_15_out), .in1(Line2Mem2), .out(Line2MemOut), .sel(Active2));
  and and_10 (Active2, multiplexer_16_out, Active);
  Way way0 (
    .Active(Active0), .OffsetBits(OffsetBits), .SetBits(SetBits), .TagBits(TagBits),
    .didContain(DidContainOut), .Write(Write), .ClearDirty(ClearDirty), .IncomingData(IncomingData),
    .CpuWriteValueIn(CpuWriteValueIn), .LineFromMemIn(LineFromMemIn), .ClkIn(ClkIn),
    .CurrTagBits(CurrTagBits0), .Valid(Valid0), .Dirty(Dirty0), .ByteReadOut(ByteReadOut0),
    .MemAddressOut(MemAddress0), .Line2MemOut(Line2Mem0));
  Way way2 (
    .Active(Active2), .OffsetBits(OffsetBits), .SetBits(SetBits), .TagBits(TagBits),
    .didContain(DidContainOut), .Write(Write), .ClearDirty(ClearDirty), .IncomingData(IncomingData),
    .CpuWriteValueIn(CpuWriteValueIn), .LineFromMemIn(LineFromMemIn), .ClkIn(ClkIn),
    .CurrTagBits(CurrTagBits2), .Valid(Valid2), .Dirty(Dirty2), .ByteReadOut(ByteReadOut2),
    .MemAddressOut(MemAddress2), .Line2MemOut(Line2Mem2));
  Way way1 (
    .Active(Active1), .OffsetBits(OffsetBits), .SetBits(SetBits), .TagBits(TagBits),
    .didContain(DidContainOut), .Write(Write), .ClearDirty(ClearDirty), .IncomingData(IncomingData),
    .CpuWriteValueIn(CpuWriteValueIn), .LineFromMemIn(LineFromMemIn), .ClkIn(ClkIn),
    .CurrTagBits(CurrTagBits1), .Valid(Valid1), .Dirty(Dirty1), .ByteReadOut(ByteReadOut1),
    .MemAddressOut(MemAddress1), .Line2MemOut(Line2Mem1));

  // Other names for the same wires on the sheet: ByteRead[7:0] = ByteReadOut; clk = ClkIn; CpuRead = CpuReadIn;
  //   CpuWrite = CpuWriteIn; CpuWriteValue[7:0] = CpuWriteValueIn; DidContain = DidContainOut;
  //   Line2Mem[31:0] = Line2MemOut; LineFromMem[31:0] = LineFromMemIn; MemAddress[7:0] = MemAddressOut

  // Notes on the sheet:
  //   address is in Cache (didContain = 1)
  //   Address is not in Cache, find which way to go to (didContain = 0)
endmodule

module Way (
  input  Active,
  input  [1:0] OffsetBits,
  input  SetBits,
  input  [6:0] TagBits,
  input  didContain,
  input  Write,
  input  ClearDirty,
  input  IncomingData,
  input  [7:0] CpuWriteValueIn,
  input  [31:0] LineFromMemIn,
  input  ClkIn,
  output [6:0] CurrTagBits,
  output Valid,
  output Dirty,
  output [7:0] ByteReadOut,
  output [7:0] MemAddressOut,
  output [31:0] Line2MemOut
);

  wire and_1_out, and_2_out, and_3_out, and_5_out, EnableByte, multiplexer_1_out, multiplexer_2_out,
       multiplexer_3_out, not_1_out, or_1_out, or_2_out, Write0, Write1, Write2, Write3;
  wire [7:0] multiplexer_4_out, multiplexer_5_out, multiplexer_6_out, multiplexer_7_out, multiplexer_8_out,
       multiplexer_9_out, multiplexer_10_out, multiplexer_11_out;

  Multiplexer #(.enable("false")) multiplexer_1 (.in0(Write), .in1(1'b0), .out(multiplexer_1_out), .sel(IncomingData));
  Register #(.width(1)) ValidReg (.D(1'b1), .en(and_1_out), .clk(ClkIn), .Q(Valid));  // open: clr
  and and_1 (and_1_out, Active, Write);
  Multiplexer #(.enable("false")) multiplexer_2 (
    .in0(Dirty), .in1(multiplexer_1_out), .out(multiplexer_2_out), .sel(Write));
  or or_1 (or_1_out, ClearDirty, Write);
  and and_2 (and_2_out, Active, Write);
  Multiplexer #(.enable("false")) multiplexer_3 (
    .in0(multiplexer_2_out), .in1(1'b0), .out(multiplexer_3_out), .sel(ClearDirty));
  and and_3 (and_3_out, Active, or_1_out);
  Register #(.width(7)) TagReg (.D(TagBits), .en(and_2_out), .clk(ClkIn), .Q(CurrTagBits));  // open: clr
  Register #(.width(1)) DirtyReg (.D(multiplexer_3_out), .en(and_3_out), .clk(ClkIn), .Q(Dirty));  // open: clr
  Multiplexer #(.enable("false"), .width(8)) multiplexer_4 (
    .in0(Line2MemOut[15:8]), .in1(LineFromMemIn[15:8]), .out(multiplexer_4_out), .sel(IncomingData));
  Multiplexer #(.enable("false"), .width(8)) multiplexer_5 (
    .in0(Line2MemOut[23:16]), .in1(LineFromMemIn[23:16]), .out(multiplexer_5_out), .sel(IncomingData));
  Multiplexer #(.enable("false"), .width(8)) multiplexer_6 (
    .in0(Line2MemOut[31:24]), .in1(LineFromMemIn[31:24]), .out(multiplexer_6_out), .sel(IncomingData));
  or or_2 (or_2_out, Write, IncomingData);
  Multiplexer #(.enable("false"), .width(8)) multiplexer_7 (
    .in0(Line2MemOut[7:0]), .in1(LineFromMemIn[7:0]), .out(multiplexer_7_out), .sel(IncomingData));
  Multiplexer #(.enable("false"), .width(8)) multiplexer_8 (
    .in0(multiplexer_7_out), .in1(CpuWriteValueIn), .out(multiplexer_8_out), .sel(Write0));
  Multiplexer #(.enable("false"), .width(8)) multiplexer_9 (
    .in0(multiplexer_4_out), .in1(CpuWriteValueIn), .out(multiplexer_9_out), .sel(Write1));
  Multiplexer #(.enable("false"), .width(8)) multiplexer_10 (
    .in0(multiplexer_5_out), .in1(CpuWriteValueIn), .out(multiplexer_10_out), .sel(Write2));
  Multiplexer #(.enable("false"), .width(8)) multiplexer_11 (
    .in0(multiplexer_6_out), .in1(CpuWriteValueIn), .out(multiplexer_11_out), .sel(Write3));
  and and_4 (EnableByte, Active, or_2_out);
  Register byte0 (.D(multiplexer_8_out), .en(EnableByte), .clk(ClkIn), .Q(Line2MemOut[7:0]));  // open: clr
  Register byte1 (.D(multiplexer_9_out), .en(EnableByte), .clk(ClkIn), .Q(Line2MemOut[15:8]));  // open: clr
  Register byte2 (.D(multiplexer_10_out), .en(EnableByte), .clk(ClkIn), .Q(Line2MemOut[23:16]));  // open: clr
  Register byte3 (.D(multiplexer_11_out), .en(EnableByte), .clk(ClkIn), .Q(Line2MemOut[31:24]));  // open: clr
  Multiplexer #(.enable("false"), .width(8)) multiplexer_12 (
    .in0({TagBits, SetBits}), .in1({CurrTagBits, SetBits}), .out(MemAddressOut), .sel(ClearDirty));
  not not_1 (not_1_out, IncomingData);
  and and_5 (and_5_out, Write, not_1_out);
  Demultiplexer #(.enable("false"), .select(2)) demultiplexer_1 (
    .out0(Write0), .out1(Write1), .out2(Write2), .out3(Write3), .in(and_5_out), .sel(OffsetBits));
  Multiplexer #(.enable("false"), .select(2), .width(8)) multiplexer_13 (
    .in0(Line2MemOut[7:0]), .in1(Line2MemOut[15:8]), .in2(Line2MemOut[23:16]), .in3(Line2MemOut[31:24]),
    .out(ByteReadOut), .sel(OffsetBits));

  // Other names for the same wires on the sheet: ByteRead[7:0] = ByteReadOut; clk = ClkIn;
  //   CpuWriteValue[7:0] = CpuWriteValueIn; byte0out[7:0] = Line2MemOut[7:0]; Line2Mem[31:0] = Line2MemOut;
  //   byte1out[7:0] = Line2MemOut[15:8]; byte2out[7:0] = Line2MemOut[23:16]; byte3out[7:0] = Line2MemOut[31:24];
  //   byte0FromMem[7:0] = LineFromMemIn[7:0]; LineFromMem[31:0] = LineFromMemIn;
  //   byte1FromMem[7:0] = LineFromMemIn[15:8]; byte2FromMem[7:0] = LineFromMemIn[23:16];
  //   byte3FromMem[7:0] = LineFromMemIn[31:24]; MemAddress[7:0] = MemAddressOut; MemAddressWrite = ClearDirty
endmodule

module FSMController (
  input  CpuRead,
  input  CpuWrite,
  input  didContain,
  input  Dirty,
  input  ClkIn,
  output Ready,
  output Initialize,
  output MemReadOut,
  output MemWriteOut,
  output UpdateAge,
  output IncomingData,
  output WriteOut
);

  wire [2:0] nextstate_1_nextstate, register_1_q;

  NextState nextstate_1 (
    .CurrentState(register_1_q), .Read(CpuRead), .Write(CpuWrite), .didContain(didContain), .Dirty(Dirty),
    .NextState(nextstate_1_nextstate));
  Register #(.width(3)) register_1 (.D(nextstate_1_nextstate), .clk(ClkIn), .Q(register_1_q));  // open: en, clr
  FSMOutput fsmoutput_1 (
    .State(register_1_q), .Ready(Ready), .Initialize(Initialize), .MemReadOut(MemReadOut),
    .MemWriteOut(MemWriteOut), .UpdateAge(UpdateAge), .IncomingData(IncomingData), .Write(WriteOut));

  // Other names for the same wires on the sheet: clk = ClkIn; CpuReadIn = CpuRead; CpuWriteIn = CpuWrite;
  //   Write = WriteOut
endmodule

module FSMOutput (
  input  [2:0] State,
  output Ready,
  output Initialize,
  output MemReadOut,
  output MemWriteOut,
  output UpdateAge,
  output IncomingData,
  output Write
);

  wire and_5_out, and_6_out, and_8_out, and_9_out, not_1_out, not_2_out, not_3_out;

  not not_1 (not_1_out, State[2]);
  not not_2 (not_2_out, State[1]);
  not not_3 (not_3_out, State[0]);
  and and_1 (Ready, not_1_out, not_2_out, not_3_out);
  and and_2 (Initialize, not_1_out, not_2_out, State[0]);
  and and_3 (MemReadOut, State[2], State[1], not_3_out);
  and and_4 (MemWriteOut, not_1_out, State[1], not_3_out);
  and and_5 (and_5_out, not_1_out, State[0]);
  and and_6 (and_6_out, State[1], State[0]);
  and and_7 (IncomingData, State[2], not_2_out, not_3_out);
  and and_8 (and_8_out, State[2], not_2_out, not_3_out);
  and and_9 (and_9_out, State[2], State[1], State[0]);
  or or_1 (UpdateAge, and_5_out, and_6_out);
  or or_2 (Write, and_8_out, and_9_out);
endmodule

module NextState (
  input  [2:0] CurrentState,
  input  Read,
  input  Write,
  input  didContain,
  input  Dirty,
  output [2:0] NextState
);

  wire and_1_out, and_2_out, and_3_out, and_4_out, and_5_out, and_6_out, and_7_out, and_8_out, and_9_out,
       and_10_out, not_1_out, not_2_out, not_3_out, not_4_out, not_5_out, not_6_out;

  not not_1 (not_1_out, CurrentState[2]);
  not not_2 (not_2_out, CurrentState[1]);
  not not_3 (not_3_out, CurrentState[0]);
  not not_4 (not_4_out, Read);
  not not_5 (not_5_out, didContain);
  not not_6 (not_6_out, Dirty);
  and and_1 (and_1_out, not_2_out, CurrentState[0], not_5_out, not_6_out);
  and and_2 (and_2_out, not_2_out, CurrentState[0], not_4_out, didContain);
  and and_3 (and_3_out, CurrentState[1], not_3_out);
  and and_4 (and_4_out, CurrentState[2], not_3_out, not_4_out);
  and and_5 (and_5_out, not_2_out, CurrentState[0]);
  and and_6 (and_6_out, not_1_out, CurrentState[1], not_3_out);
  or or_1 (NextState[1], and_5_out, and_6_out, and_7_out);
  and and_7 (and_7_out, CurrentState[2], not_2_out);
  and and_8 (and_8_out, not_2_out, not_3_out, Write);
  and and_9 (and_9_out, not_2_out, not_3_out, Read);
  or or_2 (NextState[0], and_8_out, and_9_out, and_10_out);
  and and_10 (and_10_out, not_2_out, CurrentState[0], didContain);
  or or_3 (NextState[2], and_1_out, and_2_out, and_3_out, and_4_out);
endmodule

module AgeAccessedLogic (
  input  [1:0] AgeOfAccessed,
  input  [1:0] Age0,
  input  [1:0] Age1,
  input  [1:0] Age2,
  output [1:0] Age0Out,
  output [1:0] Age1Out,
  output [1:0] Age2Out
);

  wire and_1_out, and_2_out, and_3_out, and_4_out, and_5_out, and_6_out, and_7_out, and_8_out, and_9_out,
       and_10_out, and_11_out, and_12_out, and_13_out, and_14_out, and_15_out, and_16_out, and_17_out,
       and_18_out, and_19_out, not_1_out, not_2_out, not_3_out, not_4_out, not_5_out, not_6_out, not_7_out;

  not not_1 (not_1_out, AgeOfAccessed[1]);
  not not_2 (not_2_out, AgeOfAccessed[0]);
  not not_3 (not_3_out, Age0[1]);
  not not_4 (not_4_out, Age0[0]);
  not not_5 (not_5_out, Age1[1]);
  not not_6 (not_6_out, Age2[1]);
  not not_7 (not_7_out, Age2[0]);
  and and_1 (and_1_out, not_1_out, Age0[1]);
  and and_2 (and_2_out, AgeOfAccessed[1], Age0[0]);
  and and_3 (and_3_out, not_1_out, not_2_out, Age0[0]);
  and and_4 (and_4_out, AgeOfAccessed[0], not_3_out, not_4_out);
  and and_5 (and_5_out, AgeOfAccessed[1], not_3_out, not_4_out);
  and and_6 (and_6_out, not_1_out, Age1[1]);
  and and_7 (and_7_out, AgeOfAccessed[1], not_4_out, not_7_out);
  and and_8 (and_8_out, not_1_out, not_2_out, not_4_out, not_7_out);
  and and_9 (and_9_out, AgeOfAccessed[0], not_5_out, Age2[0]);
  and and_10 (and_10_out, AgeOfAccessed[0], Age0[0], not_5_out);
  and and_11 (and_11_out, AgeOfAccessed[1], not_5_out, Age2[0]);
  and and_12 (and_12_out, AgeOfAccessed[1], Age0[0], not_5_out);
  and and_13 (and_13_out, not_1_out, not_3_out, not_5_out);
  and and_14 (and_14_out, AgeOfAccessed[1], Age2[0]);
  and and_15 (and_15_out, not_1_out, not_2_out, Age2[0]);
  and and_16 (and_16_out, AgeOfAccessed[0], Age1[0], not_6_out);
  and and_17 (and_17_out, AgeOfAccessed[0], Age0[0], not_6_out);
  and and_18 (and_18_out, AgeOfAccessed[1], Age1[0], not_6_out);
  and and_19 (and_19_out, AgeOfAccessed[1], Age0[0], not_6_out);
  or or_1 (Age0Out[1], and_1_out, and_2_out);
  or or_2 (Age0Out[0], and_3_out, and_4_out, and_5_out);
  or or_3 (Age1Out[1], and_6_out, and_7_out);
  or or_4 (Age1Out[0], and_8_out, and_9_out, and_10_out, and_11_out, and_12_out);
  or or_5 (Age2Out[1], and_13_out, and_14_out);
  or or_6 (Age2Out[0], and_15_out, and_16_out, and_17_out, and_18_out, and_19_out);
endmodule
